// Logisim project MultRepeatedAdder.circ as structural Verilog: 3 circuits, main circuit main
module main (
  input  [31:0] Input_A,
  input  [31:0] Input_B,
  input  Reset,
  output [31:0] Product,
  output Stall_Pipeline
);

  wire Clock_out;

  Clock Clock (.out(Clock_out));
  Mult mult_1 (
    .A(Input_A), .B(Input_B), .Clock(Clock_out), .Reset(Reset), .Product(Product),
    .Stall_Pipeline(Stall_Pipeline));
endmodule

module Mult (
  input  [31:0] A,
  input  [31:0] B,
  input  Clock,
  input  Reset,
  output [31:0] Product,
  output Stall_Pipeline
);

  wire and_1_out, countupto_1_iscounting;
  wire [31:0] adder_1_out;

  Adder #(.width(32)) adder_1 (.a(A), .b(Product), .out(adder_1_out));  // open: cin, cout
  Register #(.width(32)) register_1 (.D(adder_1_out), .Q(Product), .clk(Clock));  // open: en, clr
  CountUpTo countupto_1 (.Reset(Reset), .Limit(B), .IsCounting(countupto_1_iscounting), .Clock(Clock));
  and and_1 (and_1_out, 1'b1, countupto_1_iscounting);

  // Other names for the same wires on the sheet: clk = Clock; shouldStall = Stall_Pipeline

  // Notes on the sheet:
  //   INPUTS
  //   IMPLEMENT A*B
  //   OUTPUTS
endmodule

module CountUpTo (
  input  Reset,
  input  Clock,
  input  [31:0] Limit,
  output IsCounting
);

  wire comparator_1_eq, comparator_1_lt;
  wire [31:0] counter_1_q;

  Counter #(.width(32), .max('hffffffff)) counter_1 (
    .Q(counter_1_q), .clk(Clock), .clr(Reset));  // open: load, D, count, carry
  Comparator #(.width(32), .mode("unsigned")) comparator_1 (
    .a(counter_1_q), .b(Limit), .eq(comparator_1_eq), .lt(comparator_1_lt));  // open: gt
  or or_1 (IsCounting, comparator_1_eq, comparator_1_lt);

  // Other names for the same wires on the sheet: clk = Clock; rst = Reset

  // Notes on the sheet:
  //   INPUTS
  //   IMPLEMENT
  //   OUTPUTS
endmodule
