// Logisim project Lab7.circ as structural Verilog: 7 circuits, main circuit main
module main (
  output [7:0] out_1,
  output [7:0] out_2
);

  AddMachine addmachine_1 (.out_1(out_1), .out_2(out_2));
endmodule

module \nor  (
  input  in_1,
  input  in_2,
  output out_3
);

  wire or_1_out;

  or or_1 (or_1_out, in_1, in_2);
  // NOT_Gate not_1: pin names not known; wires that end beside it: or_1_out, out_3
endmodule

module AddMachine (
  output [7:0] out_1,
  output [7:0] out_2
);

  wire clock_1_out;

  Adder adder_1 (.a(out_1), .b(8'h1), .out(out_2));  // open: cin, cout
  Register register_1 (.D(out_2), .Q(out_1), .clk(clock_1_out), .clr(clock_1_out));  // open: en
  Clock clock_1 (.out(clock_1_out));
endmodule

module \nand  (
  input  in_1,
  input  in_2,
  output out_3
);

  wire and_1_out;

  and and_1 (and_1_out, in_1, in_2, in_2);
  // NOT_Gate not_1: pin names not known; wires that end beside it: and_1_out, out_3
endmodule

module \xor  (
  input  in_1,
  input  in_2,
  output out_3
);

  wire and_1_p4, not_1_p2, or_1_out;

  // AND_Gate and_1: pin names not known; wires that end beside it: in_1, in_1, in_2, and_1_p4
  // NOT_Gate not_1: pin names not known; wires that end beside it: and_1_p4, not_1_p2
  or or_1 (or_1_out, in_2, in_1);
  and and_2 (out_3, not_1_p2, or_1_out);
endmodule

module _2_1_mult (
  input  in_1,
  input  in_2,
  input  in_3,
  output out_4
);

  wire and_1_out, and_2_out, not_1_p2;

  // NOT_Gate not_1: pin names not known; wires that end beside it: in_3, not_1_p2
  and and_1 (and_1_out, not_1_p2, in_1);
  and and_2 (and_2_out, in_3, in_2);
  or or_1 (out_4, and_1_out, and_2_out);
endmodule

module _4_1_mult (
  input  in_1,
  input  in_2,
  input  in_3,
  input  in_4,
  input  in_5,
  input  in_6,
  output out_7
);

  wire and_1_out, and_2_out, and_3_out, and_4_out, not_1_p2, not_2_p2;

  // NOT_Gate not_1: pin names not known; wires that end beside it: in_1, not_1_p2
  // NOT_Gate not_2: pin names not known; wires that end beside it: in_3, not_2_p2
  and and_1 (and_1_out, not_1_p2, not_2_p2, in_2);
  and and_2 (and_2_out, in_1, not_2_p2, in_4);
  and and_3 (and_3_out, not_1_p2, in_3, in_5);
  and and_4 (and_4_out, in_3, in_1, in_6);
  or or_1 (out_7, and_1_out, and_2_out, and_3_out, and_4_out);
endmodule
