// Logisim project Lab8.circ as structural Verilog: 4 circuits, main circuit main
module main (
  input  [15:0] in_1,
  input  [15:0] in_2,
  input  [3:0] in_3,
  input  [3:0] in_4,
  input  [15:0] in_5,
  input  [15:0] in_6,
  input  [3:0] in_7,
  input  [3:0] in_8,
  output [15:0] out_9,
  output [15:0] out_10,
  output [15:0] out_11,
  output [15:0] out_12
);

  rotr rotr_1 (.in_1(in_1), .in_2(in_3), .out_3(out_9));
  rotr rotr_2 (.in_1(in_5), .in_2(in_7), .out_3(out_11));
  rotr rotr_3 (.in_1(in_2), .in_2(in_4), .out_3(out_10));
  rotr rotr_4 (.in_1(in_6), .in_2(in_8), .out_3(out_12));

  // Notes on the sheet:
  //   test1
  //   test3
  //   test2
  //   test4
endmodule

module Ex1 (
  input  [7:0] in_1,
  output out1,
  output [7:0] out2
);

  // NOT_Gate not_1: pin names not known; wires that end beside it: in_1[7], out2[7]
  and and_1 (out1, in_1[0], in_1[7]);

  assign out2[6:0] = in_1[6:0];
endmodule

module rotr (
  input  [15:0] in_1,
  input  [3:0] in_2,
  output [15:0] out_3
);

  wire Clock, comparator_1_eq, comparator_1_gt, comparator_1_lt, comparator_2_eq, comparator_2_lt,
       counter_1_q, or_1_out, or_2_out, Run, Run_t, sr1_bit_discarded;
  wire [3:0] counter_2_q;
  wire [4:0] counter_3_q;
  wire [15:0] multiplexer_1_out, register_1_q, register_2_q, sr1_2_out_4, sr1_out_4;

  Counter #(.width(1), .max('h1), .ongoal("stay")) counter_1 (
    .Q(counter_1_q), .clk(Clock));  // open: load, D, count, carry, clr
  Clock clock_1 (.out(Clock));
  Counter #(.width(4), .max('hf), .ongoal("stay")) counter_2 (
    .Q(counter_2_q), .clk(Clock));  // open: load, D, count, carry, clr
  Comparator #(.width(4), .mode("unsigned")) comparator_1 (
    .a(counter_2_q), .b(in_2), .gt(comparator_1_gt), .eq(comparator_1_eq), .lt(comparator_1_lt));
  Counter #(.width(5), .max('h10), .ongoal("stay")) counter_3 (
    .Q(counter_3_q), .clk(Clock));  // open: load, D, count, carry, clr
  Comparator #(.width(5), .mode("unsigned")) comparator_2 (
    .a(counter_3_q), .b(5'b01111), .eq(comparator_2_eq), .lt(comparator_2_lt));  // open: gt
  Register #(.width(16)) register_1 (.D(multiplexer_1_out), .Q(register_1_q), .clk(Run));  // open: en, clr
  Multiplexer #(.width(16)) multiplexer_1 (
    .in0(in_1), .in1(sr1_out_4), .out(multiplexer_1_out), .sel(counter_1_q));  // open: en
  or or_1 (or_1_out, comparator_1_gt, comparator_1_eq, comparator_1_lt);
  or or_2 (or_2_out, comparator_2_eq, comparator_2_eq, comparator_2_lt);
  sr1 sr1 (.in_1(register_1_q), .in_2(1'b0), .bit_discarded(sr1_bit_discarded), .out_4(sr1_out_4));
  and and_1 (Run, Clock, or_2_out, or_1_out);
  Register #(.width(16)) register_2 (.D(sr1_2_out_4), .Q(register_2_q), .clk(Run_t));  // open: en, clr
  sr1 sr1_2 (.in_1(register_2_q), .in_2(sr1_bit_discarded), .out_4(sr1_2_out_4));  // open: bit_discarded
  assign out_3 = register_2_q | register_1_q;  // OR_Gate or_3, 16 bits wide

  // Notes on the sheet:
  //   Starting bits
  //   Loop
  //   Number of bits to rotate
  //   Special case stop condition for (1111)
  //   bits to be rotated
endmodule

module sr1 (
  input  [15:0] in_1,
  input  in_2,
  output bit_discarded,
  output [15:0] out_4
);


  assign bit_discarded = in_1[0];
  assign out_4 = {in_2, in_1[15:1]};

  // Notes on the sheet:
  //   Shifts the input right 1
  //   Adds the input 0 or 1 to the left
  //   shifted bits
endmodule
