// Logisim project ALU.circ as structural Verilog: 1 circuit, main circuit ALU
// LAB12-ALU
module ALU (
  input  [31:0] ALU_Source_1,
  input  [31:0] ALU_Source_2,
  input  [2:0] ALU_Control,
  output [31:0] ALU_Result
);

  wire [4:0] bit_extender_1_out;
  wire [31:0] and_1_out, or_1_out, shifter_1_out, shifter_2_out, shifter_3_out, shifter_4_out, shifter_5_out,
       xor_1_out;

  // Probe on ALU_Source_1
  // Probe on ALU_Source_2
  Shifter #(.width(32)) shifter_1 (.in(ALU_Source_1), .\dist (bit_extender_1_out), .out(shifter_1_out));
  Bit_Extender #(.in_width(32), .out_width(5)) bit_extender_1 (.in(ALU_Source_2), .out(bit_extender_1_out));
  Multiplexer #(.select(3), .width(32)) multiplexer_1 (
    .in0(shifter_1_out), .in1(shifter_2_out), .in2(shifter_3_out), .in3(shifter_4_out), .in4(shifter_5_out),
    .in5(and_1_out), .in6(or_1_out), .in7(xor_1_out), .out(ALU_Result), .sel(ALU_Control));  // open: en
  Shifter #(.width(32), .shift("lr")) shifter_2 (.in(ALU_Source_1), .\dist (bit_extender_1_out), .out(shifter_2_out));
  Shifter #(.width(32), .shift("ar")) shifter_3 (.in(ALU_Source_1), .\dist (bit_extender_1_out), .out(shifter_3_out));
  assign xor_1_out = ALU_Source_1 ^ ALU_Source_2;  // XOR_Gate xor_1, 32 bits wide
  Shifter #(.width(32), .shift("rl")) shifter_4 (.in(ALU_Source_1), .\dist (bit_extender_1_out), .out(shifter_4_out));
  assign or_1_out = ALU_Source_1 | ALU_Source_2;  // OR_Gate or_1, 32 bits wide
  assign and_1_out = ALU_Source_1 & ALU_Source_2;  // AND_Gate and_1, 32 bits wide
  Shifter #(.width(32), .shift("rr")) shifter_5 (.in(ALU_Source_1), .\dist (bit_extender_1_out), .out(shifter_5_out));
  // Probe on ALU_Result

  // Other names for the same wires on the sheet: control[2:0] = ALU_Control; result[31:0] = ALU_Result;
  //   source1[31:0] = ALU_Source_1; source2[31:0] = ALU_Source_2

  // Notes on the sheet:
  //   DO NOT CROSS WIRES
  //   OVER THIS BOX
  //   DO NOT CROSS WIRES
  //   OVER THIS BOX
  //   COMPUTE ALL POSSIBLE OPERATIONS
  //   DO NOT CROSS WIRES
  //   OVER THIS BOX
  //   DO NOT CROSS WIRES
  //   OVER THIS BOX
  //   SELECT THE REQUESTED RESULT
  //   * YOUR CIRCUIT HERE *
  //   DO NOT CROSS WIRES
  //   OVER THIS BOX
endmodule
