// Logisim project alu.circ as structural Verilog: 1 circuit, main circuit main
module main (
  input  [15:0] X,
  input  [15:0] Y,
  input  [2:0] Switch,
  output Equal,
  output [15:0] Result,
  output [15:0] Result_2
);

  wire slt;
  wire [3:0] bit_extender_1_out, bit_extender_2_out;
  wire [15:0] add, \and , bit_extender_3_out, ml, \or , sll, srl, \xor ;

  Shifter #(.width(16)) shifter_1 (.in(X), .\dist (bit_extender_1_out), .out(sll));
  Bit_Extender #(.in_width(16), .out_width(4)) bit_extender_1 (.in(Y), .out(bit_extender_1_out));
  Adder #(.width(16)) adder_1 (.a(X), .b(Y), .out(add));  // open: cin, cout
  Multiplier #(.width(16)) multiplier_1 (.a(X), .b(Y), .out(ml), .cout(Result_2));  // open: cin
  Bit_Extender #(.in_width(16), .out_width(4)) bit_extender_2 (.in(Y), .out(bit_extender_2_out));
  Shifter #(.width(16), .shift("lr")) shifter_2 (.in(X), .\dist (bit_extender_2_out), .out(srl));
  assign \and  = X & Y;  // AND_Gate and_1, 16 bits wide
  assign \or  = X | Y;  // OR_Gate or_1, 16 bits wide
  assign bit_extender_3_out = {{15{1'b0}}, slt};  // Bit_Extender bit_extender_3
  assign \xor  = X ^ Y;  // XOR_Gate xor_1, 16 bits wide
  Multiplexer #(.select(3), .width(16), .enable("false")) multiplexer_1 (
    .in0(sll), .in1(srl), .in2(add), .in3(\and ), .in4(\or ), .in5(\xor ), .in6(bit_extender_3_out),
    .in7(ml), .out(Result), .sel(Switch));
  Comparator #(.width(16)) comparator_1 (.a(X), .b(Y), .eq(Equal), .lt(slt));  // open: gt

  // Other names for the same wires on the sheet: S[2:0] = Switch

  // Notes on the sheet:
  //   INPUTS to your circuit
  //   DON'T CHANGE THE LOCATIONS OF THE INPUTS AND OUTPUTS!
  //   OUTPUTS from your circuit
endmodule
