// Logisim project regfile.circ as structural Verilog: 1 circuit, main circuit main
module main (
  input  [2:0] Read_Register_1,
  input  [2:0] Read_Register_2,
  input  [2:0] Write_Register,
  input  [15:0] Write_Data,
  input  Write_Enable,
  input  Clock,
  output [15:0] s0_Value,
  output [15:0] s1_Value,
  output [15:0] s2_Value,
  output [15:0] ra_Value,
  output [15:0] sp_Value,
  output [15:0] Read_Data_1,
  output [15:0] Read_Data_2
);

  wire write_ena0, write_enRa, write_ens0, write_ens1, write_ens2, write_ensp, write_env0;
  wire [15:0] a0, v0;

  Register #(.width(16)) register_1 (.D(Write_Data), .en(write_enRa), .Q(ra_Value), .clk(Clock));  // open: clr
  Register #(.width(16)) register_2 (.D(Write_Data), .en(write_ens0), .Q(s0_Value), .clk(Clock));  // open: clr
  Register #(.width(16)) register_3 (.D(Write_Data), .en(write_ens1), .Q(s1_Value), .clk(Clock));  // open: clr
  Register #(.width(16)) register_4 (.D(Write_Data), .en(write_ens2), .Q(s2_Value), .clk(Clock));  // open: clr
  Demultiplexer #(.select(3), .enable("false")) demultiplexer_1 (
    .out1(write_enRa), .out2(write_ens0), .out3(write_ens1), .out4(write_ens2), .out5(write_ena0),
    .out6(write_env0), .out7(write_ensp), .in(Write_Enable), .sel(Write_Register));  // open: out0
  Register #(.width(16)) register_5 (.D(Write_Data), .en(write_ena0), .Q(a0), .clk(Clock));  // open: clr
  Register #(.width(16)) register_6 (.D(Write_Data), .en(write_env0), .Q(v0), .clk(Clock));  // open: clr
  Register #(.width(16)) register_7 (.D(Write_Data), .en(write_ensp), .Q(sp_Value), .clk(Clock));  // open: clr
  Multiplexer #(.select(3), .width(16), .enable("false")) multiplexer_1 (
    .in0({16{1'b0}}), .in1(ra_Value), .in2(s0_Value), .in3(s1_Value), .in4(s2_Value), .in5(a0), .in6(v0),
    .in7(sp_Value), .out(Read_Data_1), .sel(Read_Register_1));
  Multiplexer #(.select(3), .width(16), .enable("false")) multiplexer_2 (
    .in0({16{1'b0}}), .in1(ra_Value), .in2(s0_Value), .in3(s1_Value), .in4(s2_Value), .in5(a0), .in6(v0),
    .in7(sp_Value), .out(Read_Data_2), .sel(Read_Register_2));

  // Other names for the same wires on the sheet: clk = Clock; ra[15:0] = ra_Value; read_data1[15:0] = Read_Data_1;
  //   read_data2[15:0] = Read_Data_2; read_reg1[2:0] = Read_Register_1; read_reg2[2:0] = Read_Register_2;
  //   s0[15:0] = s0_Value; s1[15:0] = s1_Value; s2[15:0] = s2_Value; sp[15:0] = sp_Value; write_en = Write_Enable;
  //   write_reg[2:0] = Write_Register

  // Notes on the sheet:
  //   INPUTS to your circuit
  //   DON'T CHANGE THE LOCATIONS OF THE INPUTS AND OUTPUTS!
  //   These are DEBUG/TEST outputs from your circuit.
  //   OUTPUTS from your circuit
endmodule
