// Logisim project cpu.circ as structural Verilog: 1 circuit, main circuit main
module main (
  input  [15:0] INSTRUCTION,
  input  CLOCK,
  output [15:0] FETCH_ADDRESS,
  output [15:0] s0_Value,
  output [15:0] s1_Value,
  output [15:0] s2_Value,
  output [15:0] ra_Value,
  output [15:0] sp_Value,
  output [15:0] HI_Value,
  output [15:0] LO_Value
);

  wire addi, and_2_out, and_3_out, andi, beq, bne, branch, equal, Hazard, j, jr, jump, lh, lui, MEM_p6, mfhi,
       mflo, mult, mult_out, not_1_out, not_2_out, not_3_out, not_4_out, not_5_out, not_6_out, not_7_out,
       not_8_out, not_9_out, not_10_out, not_11_out, not_12_out, not_13_out, not_14_out, not_15_out,
       not_16_out, not_17_out, not_18_out, not_19_out, not_20_out, not_21_out, not_22_out, not_23_out,
       not_24_out, not_25_out, not_26_out, not_27_out, not_28_out, not_29_out, not_30_out, not_31_out,
       not_32_out, not_33_out, not_34_out, or_2_out, or_4_out, or_5_out, ori, r_i, r_type_out, RegWrite, sh,
       slti, swap_rd_rt, Wlo;
  wire [0:0] or_1_out;
  wire [2:0] Aluctl, bit_extender_1_out, funct, ictl, multiplexer_7_out, multiplexer_8_out, multiplexer_9_out;
  wire [2:1] register_1_q;
  wire [3:0] op;
  wire [5:3] i_imm;
  wire [9:6] u_imm;
  wire [15:0] adder_1_out, adder_2_out, bit_extender_2_out, bit_extender_3_out, data2, imm, jra,
       main_1_read_data_1, main_2_result_2, MEM_p5, multiplexer_1_out, multiplexer_2_out, multiplexer_3_out,
       multiplexer_4_out, multiplexer_12_out, multiplexer_13_out, multiplexer_14_out, multiplexer_15_out,
       multiplexer_16_out, subtractor_1_out, WriteData;

  Register #(.width(16)) PC (.D(multiplexer_3_out), .Q(FETCH_ADDRESS), .clk(CLOCK));  // open: en, clr
  Adder #(.width(16)) adder_1 (.a(FETCH_ADDRESS), .b(16'h2), .out(adder_1_out));  // open: cin, cout
  Subtractor #(.width(16)) subtractor_1 (.a(FETCH_ADDRESS), .b(16'h2), .out(subtractor_1_out));  // open: bin, bout
  Adder #(.width(16)) adder_2 (.a(subtractor_1_out), .b(imm), .out(adder_2_out));  // open: cin, cout
  Multiplexer #(.width(16), .enable("false")) multiplexer_1 (
    .in0(adder_1_out), .in1(adder_2_out), .out(multiplexer_1_out), .sel(branch));
  Multiplexer #(.width(16), .enable("false")) multiplexer_2 (
    .in0(multiplexer_1_out), .in1(jra), .out(multiplexer_2_out), .sel(jr));
  Multiplexer #(.width(16), .enable("false")) multiplexer_3 (
    .in0(multiplexer_2_out), .in1({FETCH_ADDRESS[15:10], u_imm, i_imm, funct}), .out(multiplexer_3_out),
    .sel(j));
  not not_1 (not_1_out, op[0]);
  and u_addi (addi, not_1_out, op[1], op[2], not_2_out);
  not not_2 (not_2_out, op[3]);
  not not_3 (not_3_out, op[0]);
  not not_4 (not_4_out, op[2]);
  and u_lh (lh, not_3_out, op[1], not_4_out, op[3]);
  not not_5 (not_5_out, op[2]);
  and u_sh (sh, op[0], op[1], not_5_out, op[3]);
  and u_slti (slti, op[0], op[1], op[2], not_6_out);
  not not_6 (not_6_out, op[3]);
  not not_7 (not_7_out, op[0]);
  not not_8 (not_8_out, op[1]);
  and u_andi (andi, not_7_out, not_8_out, not_9_out, op[3]);
  not not_9 (not_9_out, op[2]);
  not not_10 (not_10_out, op[1]);
  not not_11 (not_11_out, op[2]);
  and u_ori (ori, op[0], not_10_out, not_11_out, op[3]);
  or or_1 (or_1_out[0], addi, lh, sh);
  Multiplexer #(.width(16), .enable("false")) multiplexer_4 (
    .in0(INSTRUCTION), .in1({16{1'b0}}), .out(multiplexer_4_out), .sel(Hazard));
  Multiplexer #(.select(4), .width(3), .enable("false")) multiplexer_5 (
    .in0(3'b010), .in1(3'b010), .in2(3'b110), .in3(3'b110), .in4(3'b011), .in5(3'b011), .in6(3'b011),
    .in7(3'b011), .in8(3'b100), .in9(3'b100), .in10(3'b100), .in11(3'b100), .in12(3'b100), .in13(3'b100),
    .in14(3'b100), .in15(3'b100), .out(ictl), .sel({ori, andi, slti, or_1_out[0]}));
  or or_2 (or_2_out, bne, beq);
  Register #(.width(16)) register_1 (
    .D(multiplexer_4_out), .Q({op, register_1_q, u_imm, i_imm, funct}), .clk(CLOCK));  // open: en, clr
  Multiplexer #(.width(3), .enable("false")) multiplexer_6 (
    .in0(ictl), .in1(multiplexer_7_out), .out(Aluctl), .sel(r_i));
  Multiplexer #(.width(3), .enable("false")) multiplexer_7 (
    .in0(3'b010), .in1(funct), .out(multiplexer_7_out), .sel(not_12_out));
  not not_12 (not_12_out, or_2_out);
  not not_13 (not_13_out, op[0]);
  not not_14 (not_14_out, op[1]);
  not not_15 (not_15_out, op[2]);
  not not_16 (not_16_out, op[3]);
  not not_17 (not_17_out, op[0]);
  not not_18 (not_18_out, op[1]);
  not not_19 (not_19_out, op[1]);
  not not_20 (not_20_out, op[0]);
  not not_21 (not_21_out, op[1]);
  not not_22 (not_22_out, op[3]);
  not not_23 (not_23_out, op[1]);
  not not_24 (not_24_out, op[3]);
  not not_25 (not_25_out, op[2]);
  not not_26 (not_26_out, op[3]);
  and and_1 (mult, mult_out, r_type_out);
  and u_mult (mult_out, funct[0], funct[1], funct[2]);
  and r_type (r_type_out, not_13_out, not_14_out, not_15_out, not_16_out);
  and u_mfhi (mfhi, not_17_out, not_18_out, op[2], op[3]);
  and u_mflo (mflo, op[0], not_19_out, op[2], op[3]);
  and u_beq (beq, not_20_out, not_21_out, op[2], not_22_out);
  and u_bne (bne, op[0], not_23_out, op[2], not_24_out);
  and u_jr (jr, op[0], op[1], not_25_out, not_26_out);
  or or_3 (r_i, r_type_out, or_4_out);
  or or_4 (or_4_out, bne, beq);
  assign bit_extender_1_out = {{1{1'b0}}, register_1_q};  // Bit_Extender bit_extender_1
  not not_27 (not_27_out, equal);
  Multiplexer #(.width(3), .enable("false")) multiplexer_8 (
    .in0(i_imm), .in1({register_1_q, u_imm[9]}), .out(multiplexer_8_out), .sel(swap_rd_rt));
  assign bit_extender_2_out = {{10{1'b0}}, {i_imm, funct}};  // Bit_Extender bit_extender_2
  assign bit_extender_3_out = {{10{i_imm[5]}}, {i_imm, funct}};  // Bit_Extender bit_extender_3
  and and_2 (and_2_out, equal, beq);
  and and_3 (and_3_out, not_27_out, bne);
  not not_28 (not_28_out, op[1]);
  and u_lui (lui, op[0], not_28_out, not_29_out, not_30_out);
  not not_29 (not_29_out, op[2]);
  not not_30 (not_30_out, op[3]);
  not not_31 (not_31_out, op[0]);
  and u_j (j, not_31_out, op[1], not_32_out, not_33_out);
  not not_32 (not_32_out, op[2]);
  not not_33 (not_33_out, op[3]);
  Multiplexer #(.width(3), .enable("false")) multiplexer_9 (
    .in0({register_1_q, u_imm[9]}), .in1(bit_extender_1_out), .out(multiplexer_9_out), .sel(j));
  Multiplexer #(.width(16), .enable("false")) multiplexer_10 (
    .in0(bit_extender_2_out), .in1(bit_extender_3_out), .out(imm), .sel(or_5_out));
  or or_5 (or_5_out, addi, ori, jr, lh, sh, beq, bne);
  Multiplexer #(.enable("false")) multiplexer_11 (.in0(and_2_out), .in1(and_3_out), .out(branch), .sel(bne));
  regfile_main main_1 (
    .Read_Register_1(u_imm[8:6]), .Read_Register_2(multiplexer_8_out), .Write_Register(multiplexer_9_out),
    .Write_Data(WriteData), .Write_Enable(RegWrite), .Clock(CLOCK), .Read_Data_1(main_1_read_data_1),
    .Read_Data_2(data2), .s0_Value(s0_Value), .s1_Value(s1_Value), .s2_Value(s2_Value), .ra_Value(ra_Value),
    .sp_Value(sp_Value));
  nor nor_1 (RegWrite, sh, lui, beq, bne);
  or or_6 (Wlo, mult, lui);
  or or_7 (jump, j, jr);
  or or_8 (swap_rd_rt, sh, bne, beq);
  Multiplexer #(.width(16), .enable("false")) multiplexer_12 (
    .in0(data2), .in1(imm), .out(multiplexer_12_out), .sel(not_34_out));
  Multiplexer #(.width(16), .enable("false")) multiplexer_13 (
    .in0(multiplexer_12_out), .in1({u_imm, i_imm, funct, {6{1'b0}}}), .out(multiplexer_13_out), .sel(lui));
  not not_34 (not_34_out, r_i);
  alu_main main_2 (
    .Switch(Aluctl), .X(main_1_read_data_1), .Equal(equal), .Result(jra), .Y(multiplexer_13_out),
    .Result_2(main_2_result_2));
  Register #(.width(16)) LO (.D(jra), .en(Wlo), .Q(LO_Value), .clk(CLOCK));  // open: clr
  Register #(.width(16)) HI (.D(main_2_result_2), .en(mult), .Q(HI_Value), .clk(CLOCK));  // open: clr
  or or_9 (Hazard, jump, branch);
  // mem_main MEM: pin names not known; wires that end beside it: jra, data2, sh, CLOCK, MEM_p5, MEM_p6
  Multiplexer #(.width(16), .enable("false")) multiplexer_14 (
    .in0(jra), .in1(MEM_p5), .out(multiplexer_14_out), .sel(lh));
  Multiplexer #(.width(16), .enable("false")) multiplexer_15 (
    .in0(multiplexer_14_out), .in1(HI_Value), .out(multiplexer_15_out), .sel(mfhi));
  Multiplexer #(.width(16), .enable("false")) multiplexer_16 (
    .in0(multiplexer_15_out), .in1(LO_Value), .out(multiplexer_16_out), .sel(mflo));
  Multiplexer #(.width(16), .enable("false")) multiplexer_17 (
    .in0(multiplexer_16_out), .in1(FETCH_ADDRESS), .out(WriteData), .sel(jump));
  // Probe on WriteData

  // Other names for the same wires on the sheet: fetch_addr[15:0] = FETCH_ADDRESS; pc[15:0] = FETCH_ADDRESS;
  //   clk = CLOCK; hi[15:0] = HI_Value; lo[15:0] = LO_Value; ra[15:0] = ra_Value; s0[15:0] = s0_Value;
  //   s1[15:0] = s1_Value; s2[15:0] = s2_Value; sp[15:0] = sp_Value; i_imm[2:0] = funct; u_imm[5:0] = {i_imm, funct};
  //   uImmEx[15:6] = {u_imm, i_imm, funct}

  // Notes on the sheet:
  //   Output
  //   These are outputs/inputs from run.circ
  //   Inputs
  //   These are DEBUG/TEST outputs from your circuit.
  //   CONTROL UNIT
  //   funct
  //   rt
  //   rs
  //   rd
  //   op
  //   i imm
  //   u imm
  //   u rd
endmodule
